# Fritzing sketch wemos weather (saved by Fritzing 0.9.3b)

parts:
  WeMos_D1_Mini1 = WeMos D1 Mini
  Part1 = NeoPixel NeoMatrix 8x8 [part_number=1487]
  Part2 = Adafruit AT42QT1012 Standalone Toggle Capacitive Touch Sensor Breakout [part_number="Adafruit #1375"]

nets:
  3V3: WeMos_D1_Mini1.3V3, Part2.LEDA, Part2.VDD
  N1: WeMos_D1_Mini1.D5, Part1.IN
  N2: WeMos_D1_Mini1.D6, Part2.OUT
  N3: WeMos_D1_Mini1.G, Part2.GND

notes:
  Red = 5V supply
  Black = Common GND between all components
  Pink = 3.3V to power touch sensor

custom parts:
  WeMos D1 Mini: The D1 mini is a mini wifi board based on ESP-8266EX.
  NeoPixel NeoMatrix 8x8: Put on your sunglasses before wiring up this LED matrix - 64 eye-blistering RGB LEDs adorn the NeoMatrix for a blast of configurable color. Arranged in an 8x8 matrix, each pixel is individually addressable. Only one microcontroller pin is required to control all the LEDs, and you get 24 bit color for each LED.
  Adafruit AT42QT1012 Standalone Toggle Capacitive Touch Sensor Breakout: This breakout board is the simplest way to create a project with a single "toggle" capacitive touch sensor. No microcontroller is required here - just power with 1.8 to 5.5VDC and touch the pad to activate the sensor. This sensor is a toggle output type: touch-on then touch-off. That means that when a capacitive load is detected (e.g. a person touches the sensor-pad area) the red LED will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
